// Logisim project somador.circ as structural Verilog: 2 circuits, main circuit main
module main (
  input  [7:0] Entrada_B,
  input  [7:0] Entrada_A,
  output [7:0] \Saída 
);

  wire somador_completo_1_cout, somador_completo_2_cout, somador_completo_3_cout, somador_completo_4_cout,
       somador_completo_5_cout, somador_completo_6_cout, somador_completo_7_cout, somador_completo_8_cout;

  somador_completo somador_completo_1 (
    .B(Entrada_B[0]), .Cin(1'b0), .A(Entrada_A[0]), .Sum(\Saída [0]), .Cout(somador_completo_1_cout));
  somador_completo somador_completo_2 (
    .B(Entrada_B[1]), .Cin(somador_completo_1_cout), .A(Entrada_A[1]), .Sum(\Saída [1]),
    .Cout(somador_completo_2_cout));
  somador_completo somador_completo_3 (
    .B(Entrada_B[2]), .Cin(somador_completo_2_cout), .A(Entrada_A[2]), .Sum(\Saída [2]),
    .Cout(somador_completo_3_cout));
  somador_completo somador_completo_4 (
    .B(Entrada_B[3]), .Cin(somador_completo_3_cout), .A(Entrada_A[3]), .Sum(\Saída [3]),
    .Cout(somador_completo_4_cout));
  somador_completo somador_completo_5 (
    .B(Entrada_B[4]), .Cin(somador_completo_4_cout), .A(Entrada_A[4]), .Sum(\Saída [4]),
    .Cout(somador_completo_5_cout));
  somador_completo somador_completo_6 (
    .B(Entrada_B[5]), .Cin(somador_completo_5_cout), .A(Entrada_A[5]), .Sum(\Saída [5]),
    .Cout(somador_completo_6_cout));
  somador_completo somador_completo_7 (
    .B(Entrada_B[6]), .Cin(somador_completo_6_cout), .A(Entrada_A[6]), .Sum(\Saída [6]),
    .Cout(somador_completo_7_cout));
  somador_completo somador_completo_8 (
    .B(Entrada_B[7]), .Cin(somador_completo_7_cout), .A(Entrada_A[7]), .Sum(\Saída [7]),
    .Cout(somador_completo_8_cout));
  LED led_1 (.in(somador_completo_8_cout));

  // Notes on the sheet:
  //   Overflow Flag
endmodule

module somador_completo (
  input  A,
  input  B,
  input  Cin,
  output Sum,
  output Cout
);

  wire and_1_out, and_2_out, and_3_out, xor_1_out;

  xor xor_1 (xor_1_out, A, B);
  and and_1 (and_1_out, A, B);
  and and_2 (and_2_out, A, Cin);
  and and_3 (and_3_out, B, Cin);
  xor xor_2 (Sum, xor_1_out, Cin);
  or or_1 (Cout, and_1_out, and_2_out, and_3_out);
endmodule
